# Fritzing sketch 3L710_alarm_sound_IC (saved by Fritzing 0.9.3b)
breadboards: 1

parts:
  3L710 = IC, DIP package, 8 pins [chip_label=3L710]
  S1 = Square Pushbutton
  VCC1 = 4 x AAA Battery Mount
  LED1 = LED - 5mm [color="Red (633nm)" package="5 mm [THT]"]
  R1 = Resistor [tolerance=±5% resistance=150 package=THT]
  Q1_S8050(NPN) = NPN-Transistor [package="TO92 [THT]"]
  R2 = Resistor [tolerance=±5% resistance=4.7k package=THT]
  SPKR1 = Loudspeaker
  R3 = Resistor [tolerance=±5% resistance=220k package=THT]

nets:
  N1: 3L710.pin1, VCC1.-, Q1_S8050(NPN).E
  N2: 3L710.pin2, LED1.cathode
  N3: 3L710.pin5, S1.leg1, R1.Pin_1, SPKR1.pin1
  N4: 3L710.pin6, R2.Pin_0
  N5: 3L710.pin7, R3.Pin_1
  N6: 3L710.pin8, R3.Pin_0
  N7: S1.leg0, VCC1.+
  N8: LED1.anode, R1.Pin_0
  N9: Q1_S8050(NPN).B, R2.Pin_1
  N10: Q1_S8050(NPN).C, SPKR1.pin2
