# Fritzing sketch ESPWROOM02_usb_writer (saved by Fritzing 0.9.3b)
breadboards: 1

parts:
  U1 = IC, DIP package, 18 pins [chip_label="ESP WROOM02"]
  NJU7223F33 = V_REG_LD1117VXX [package=78xxl]
  U2 = mystery part, 6 pins [chip_label=USB-Serial]
  S1 = SWITCH-MOMENTARY-2 [package=tactile-pth-12mm]
  R1 = Resistor [tolerance=±5% resistance=10k package=THT]
  R2 = Resistor [tolerance=±5% resistance=10k package=THT]
  R3 = Resistor [tolerance=±5% resistance=10k package=THT]
  R4 = Resistor [tolerance=±5% resistance=10k package=THT]
  R5 = Resistor [tolerance=±5% resistance=1k package=THT]
  C1 = Ceramic Capacitor [capacitance=100nF package="100 mil [THT, multilayer]"]
  C2 = Ceramic Capacitor [capacitance=100nF package="100 mil [THT, multilayer]"]
  C3 = Electrolytic Capacitor [capacitance=47µF package="100 mil [THT, electrolytic]"]
  C4 = Electrolytic Capacitor [capacitance=47µF package="100 mil [THT, electrolytic]"]

nets:
  N1: U1.pin1, NJU7223F33.OUT, R1.Pin_0, R2.Pin_0, R3.Pin_0, R5.Pin_0, C4.+
  N2: U1.pin2, R5.Pin_1, C1.1
  N3: U1.pin6, R4.Pin_1
  N4: U1.pin7, R3.Pin_1
  N5: U1.pin8, R2.Pin_1
  N6: U1.pin9, NJU7223F33.GND, U2.pin6, S1.2, R4.Pin_0, C1.0, C2.0, C3.-, C4.-
  N7: U1.pin11, U2.pin3
  N8: U1.pin12, U2.pin2
  N9: U1.pin15, S1.1, R1.Pin_1, C2.1
  N10: NJU7223F33.IN, U2.pin4, C3.+
