# Fritzing sketch SMC0618_6alarm_soundbox (saved by Fritzing 0.9.3b)
breadboards: 1

parts:
  IC1 = IC, DIP package, 16 pins [chip_label=SMC0618]
  VCC1 = Battery
  R1 = Resistor [tolerance=±5% resistance=82k package=THT]
  R2 = Resistor [tolerance=±5% resistance=220 package=THT]
  LED1 = LED - 5mm [color="Red (633nm)" package="5 mm [THT]"]
  J1 = Piezo Speaker
  S1 = Round Pushbutton
  S2 = Round Pushbutton
  S3 = Round Pushbutton
  S4 = Round Pushbutton
  S5 = Round Pushbutton
  S6 = Round Pushbutton
  R3 = Resistor [tolerance=±5% resistance=220 package=THT]
  LED2 = LED - 5mm [color="Green (570nm)" package="5 mm [THT]"]
  R4 = Rotary Potentiometer (Small) [maximum_resistance=50kΩ package=THT]

nets:
  N1: IC1.pin1, VCC1.+, S1.leg0, S2.leg0, S3.leg0, S4.leg0, S5.leg0, S6.leg0, R3.Pin_0
  N2: IC1.pin2, S1.leg1
  N3: IC1.pin3, S2.leg1
  N4: IC1.pin4, S3.leg1
  N5: IC1.pin5, S4.leg1
  N6: IC1.pin6, S5.leg1
  N7: IC1.pin7, S6.leg1
  N8: IC1.pin8, VCC1.-, LED1.cathode, J1.pin2, LED2.cathode, R4.leg1
  N9: IC1.pin11, R4.leg2
  N10: IC1.pin12, R2.Pin_0
  N11: IC1.pin13, R1.Pin_0
  N12: IC1.pin14, R1.Pin_1
  N13: R2.Pin_1, LED1.anode
  N14: J1.pin1, R4.wiper
  N15: R3.Pin_1, LED2.anode
