# Fritzing sketch UM66T_mini_emusicbox (saved by Fritzing 0.9.3b)
breadboards: 1

parts:
  U1 = mystery part, 3 pins [chip_label=UM66TxxL]
  J1 = Piezo Speaker
  BAT1 = Battery Holders [package=battcom_20mm_pth]
  S1 = SWITCH-MOMENTARY-2 [package=tactile-pth]
  LED1 = LED - 5mm [color="Red (633nm)" package="5 mm [THT]"]
  R1 = Resistor [tolerance=±5% resistance=220 package=THT]

nets:
  N1: U1.pin1, J1.pin2, BAT1.-, LED1.cathode
  N2: U1.pin2, S1.2
  N3: U1.pin3, J1.pin1
  N4: BAT1.+, S1.1, R1.Pin_0
  N5: LED1.anode, R1.Pin_1
