# Fritzing sketch bluetooth_mobile_speaker (saved by Fritzing 0.9.3b)
breadboards: 1

parts:
  946H-1C-3D_3V_relay_1_BT_CHARGER_VCC = RELAY [package=relay-t9a-2]
  18650_1_AMPBattery = LIPO-2000mAh [package=lipo-2000]
  18650_2_BTBattery = LIPO-2000mAh [package=lipo-2000]
  946H-1C-3D_3V_relay_2_BTCHARGER_VSS = RELAY [package=relay-t9a-2]
  946H-1C-3D_3V_relay_2_BTMODULE = RELAY [package=relay-t9a-2]
  POWER_SW = SWITCH-SPST-2 [package=switch-spst-vertical]
  MicroUSB_plug = USB_MICROB_PLUG [package=micro-b-ra-th]
  IC1 = IC, DIP package, 6 pins [chip_label="TP4056 CHARGER IC"]
  IC2 = IC, DIP package, 6 pins [chip_label="TP4056 CHARGER IC"]
  Step_up_regulator_5V_(AMP) = IC, DIP package, 4 pins [chip_label="Stepup regulator(5V)"]
  Step_up_regulator_5V_(BT) = IC, DIP package, 4 pins [chip_label="Stepup regulator(5V)"]
  LED1 = LED - 5mm [color="Green (570nm)" package="5 mm [THT]"]
  R1 = Resistor [tolerance=±5% resistance=220 package=THT]
  C1 = Electrolytic Capacitor [capacitance=1mF package="100 mil [THT, electrolytic]"]
  PAM8403_AMP_module = IC, DIP package, 10 pins [chip_label="PAM8403 Audio AMP"]
  SPK_L = SPEAKER [package=pcb_mount_speaker]
  SPK_R = SPEAKER [package=pcb_mount_speaker]
  X-BT_Bluetooth_receiver_module = IC, DIP package, 6 pins [chip_label=X-BT]
  C2 = Electrolytic Capacitor [capacitance=1mF package="100 mil [THT, electrolytic]"]

nets:
  3.7V_AMP_CHG_OUT+: 946H-1C-3D_3V_relay_1_BT_CHARGER_VCC.COIL1, 946H-1C-3D_3V_relay_2_BTCHARGER_VSS.COIL1, 946H-1C-3D_3V_relay_2_BTMODULE.COIL1, POWER_SW.O, Step_up_regulator_5V_(AMP).pin1, R1.Pin_0
  GND: 946H-1C-3D_3V_relay_1_BT_CHARGER_VCC.COIL2, 946H-1C-3D_3V_relay_2_BTCHARGER_VSS.COIL2, 946H-1C-3D_3V_relay_2_BTMODULE.COIL2, IC1.pin3, IC2.pin3, Step_up_regulator_5V_(AMP).pin2, Step_up_regulator_5V_(AMP).pin3, Step_up_regulator_5V_(BT).pin2, Step_up_regulator_5V_(BT).pin3, LED1.cathode, C1.-, PAM8403_AMP_module.pin5, X-BT_Bluetooth_receiver_module.pin2, C2.-
  N1: 946H-1C-3D_3V_relay_1_BT_CHARGER_VCC.MAIN, IC2.pin1
  N2: 946H-1C-3D_3V_relay_1_BT_CHARGER_VCC.NC, MicroUSB_plug.VCC, IC1.pin1
  N3: 18650_1_AMPBattery.+, IC1.pin5
  N4: 18650_1_AMPBattery.-, IC1.pin4
  N5: 18650_2_BTBattery.+, IC2.pin5
  N6: 18650_2_BTBattery.-, IC2.pin4
  N7: 946H-1C-3D_3V_relay_2_BTCHARGER_VSS.MAIN, IC2.pin2
  N8: 946H-1C-3D_3V_relay_2_BTCHARGER_VSS.NC, MicroUSB_plug.GND, IC1.pin2
  3.7V_BT_CHG_OUT+: 946H-1C-3D_3V_relay_2_BTMODULE.MAIN, Step_up_regulator_5V_(BT).pin1
  N9: 946H-1C-3D_3V_relay_2_BTMODULE.NC, IC2.pin6
  N10: POWER_SW.P, IC1.pin6
  5V_AMP: Step_up_regulator_5V_(AMP).pin4, C1.+, PAM8403_AMP_module.pin4
  5V_BT: Step_up_regulator_5V_(BT).pin4, X-BT_Bluetooth_receiver_module.pin1, C2.+
  N11: LED1.anode, R1.Pin_1
  N12: PAM8403_AMP_module.pin1, X-BT_Bluetooth_receiver_module.pin6
  N13: PAM8403_AMP_module.pin2, X-BT_Bluetooth_receiver_module.pin5
  N14: PAM8403_AMP_module.pin3, X-BT_Bluetooth_receiver_module.pin4
  N15: PAM8403_AMP_module.pin6, SPK_R.-
  N16: PAM8403_AMP_module.pin7, SPK_R.+
  N17: PAM8403_AMP_module.pin8, SPK_L.-
  N18: PAM8403_AMP_module.pin9, SPK_L.+
