# Fritzing sketch bluetooth_mobile_speaker2 (saved by Fritzing 0.9.3b)
breadboards: 1

parts:
  18650_Battery = LIPO-2000mAh [package=lipo-2000]
  POWER_SW = SWITCH-SPST-2 [package=switch-spst-vertical]
  MicroUSB_plug = USB_MICROB_PLUG [package=micro-b-ra-th]
  IC1 = IC, DIP package, 6 pins [chip_label="TP4056 CHARGER IC"]
  Step_up_regulator_5V_(for_AMP) = IC, DIP package, 4 pins [chip_label="Stepup regulator(5V)"]
  Isolated_DCDC_converter_(for_BT) = IC, DIP package, 4 pins [chip_label=MAU102]
  LED1 = LED - 5mm [color="Green (570nm)" package="5 mm [THT]"]
  R1 = Resistor [tolerance=±5% resistance=220 package=THT]
  C1 = Electrolytic Capacitor [capacitance=1mF package="100 mil [THT, electrolytic]"]
  PAM8403_AMP_module = IC, DIP package, 10 pins [chip_label="PAM8403 Audio AMP"]
  SPK_L = SPEAKER [package=pcb_mount_speaker]
  SPK_R = SPEAKER [package=pcb_mount_speaker]
  X-BT_Bluetooth_receiver_module = IC, DIP package, 6 pins [chip_label=X-BT]
  C2 = Electrolytic Capacitor [capacitance=1mF package="100 mil [THT, electrolytic]"]

nets:
  N1: 18650_Battery.+, IC1.pin5
  N2: 18650_Battery.-, IC1.pin4
  3.7V_AMP_CHG_OUT+: POWER_SW.O, Step_up_regulator_5V_(for_AMP).pin1, R1.Pin_0
  N3: POWER_SW.P, IC1.pin6
  N4: MicroUSB_plug.VCC, IC1.pin1
  N5: MicroUSB_plug.GND, IC1.pin2
  GND: IC1.pin3, Step_up_regulator_5V_(for_AMP).pin2, Step_up_regulator_5V_(for_AMP).pin3, Isolated_DCDC_converter_(for_BT).pin2, Isolated_DCDC_converter_(for_BT).pin3, LED1.cathode, C1.-, PAM8403_AMP_module.pin5, X-BT_Bluetooth_receiver_module.pin2, C2.-
  5V_AMP: Step_up_regulator_5V_(for_AMP).pin4, C1.+, PAM8403_AMP_module.pin4
  3.7V_BT_CHG_OUT+: Isolated_DCDC_converter_(for_BT).pin1
  5V_BT: Isolated_DCDC_converter_(for_BT).pin4, X-BT_Bluetooth_receiver_module.pin1, C2.+
  N6: LED1.anode, R1.Pin_1
  N7: PAM8403_AMP_module.pin1, X-BT_Bluetooth_receiver_module.pin6
  N8: PAM8403_AMP_module.pin2, X-BT_Bluetooth_receiver_module.pin5
  N9: PAM8403_AMP_module.pin3, X-BT_Bluetooth_receiver_module.pin4
  N10: PAM8403_AMP_module.pin6, SPK_R.-
  N11: PAM8403_AMP_module.pin7, SPK_R.+
  N12: PAM8403_AMP_module.pin8, SPK_L.-
  N13: PAM8403_AMP_module.pin9, SPK_L.+
