# Fritzing sketch christmas_music_tree (saved by Fritzing 0.9.3b)
breadboards: 1

parts:
  HK326-2 = IC, DIP package, 16 pins [chip_label=HK326-2]
  C1 = Electrolytic Capacitor [capacitance=2.2µF package="100 mil [THT, electrolytic]"]
  R1 = Resistor [tolerance=±5% resistance=39k package=THT]
  MODE_SW = Toggle Switch [package=THT]
  SL_SW = Toggle Switch [package=THT]
  TG_SW = Pushbutton [package="[THT]"]
  R2 = Resistor [tolerance=±5% resistance=220 package=THT]
  LED1 = LED - 5mm [color="Blue (525nm)" package="5 mm [THT]"]
  SP1 = SPEAKER [package=pcb_mount_speaker]

nets:
  N1: HK326-2.pin2, R1.Pin_1
  N2: HK326-2.pin3, C1.+
  N3: HK326-2.pin4, R1.Pin_0
  N4: HK326-2.pin5, MODE_SW.COM
  N5: HK326-2.pin6, SL_SW.COM
  N6: HK326-2.pin7, TG_SW.Pin_3, TG_SW.Pin_4
  GND: HK326-2.pin9, HK326-2.pin14, C1.-, MODE_SW.L1, SL_SW.L1, TG_SW.Pin_1, TG_SW.Pin_2
  N7: HK326-2.pin11, SP1.-
  5V: HK326-2.pin12, MODE_SW.L2, SL_SW.L2, R2.Pin_1
  N8: HK326-2.pin13, SP1.+
  N9: HK326-2.pin16, LED1.cathode
  N10: R2.Pin_0, LED1.anode
